# Fritzing sketch Turing machine (saved by Fritzing 0.9.3b)
breadboards: 1

parts:
  S1 = Momentary Switch [package=ksa_sealed_tac_switch]
  S2 = Momentary Switch [package=ksa_sealed_tac_switch]
  S3 = Momentary Switch [package=ksa_sealed_tac_switch]
  S4 = Momentary Switch [package=ksa_sealed_tac_switch]
  S5 = Momentary Switch [package=ksa_sealed_tac_switch]
  R1 = Trimmer Potentiometer [maximum_resistance=10kΩ package=THT]
  U1 = LCD-16X2 [package=lcd-16x2_noholes]
  R2 = Resistor [tolerance=±5% resistance=10k package="0402 [SMD]"]
  R6 = Resistor [tolerance=±5% resistance=10k package="0402 [SMD]"]
  R7 = Resistor [tolerance=±5% resistance=10k package="0402 [SMD]"]
  R8 = Resistor [tolerance=±5% resistance=10k package="0402 [SMD]"]
  R9 = Resistor [tolerance=±5% resistance=10k package="0402 [SMD]"]
  Part1 = Arduino Mega 2560 (Rev3)
  R10 = Resistor [tolerance=±5% resistance=220 package="0402 [SMD]"]
  R11 = Resistor [tolerance=±5% resistance=220 package="0402 [SMD]"]
  R12 = Resistor [tolerance=±5% resistance=220 package="0402 [SMD]"]
  LED2 = RGB LED (com. cathode, rgb) [package="5 mm [THT]"]
  Part2 = MicroSD Card Module
  R13 = Resistor [tolerance=±5% resistance=220 package="0402 [SMD]"]

nets:
  VDD: S1.1, S2.1, S3.1, S4.1, S5.1, R1.leg2, U1.VDD, Part1.5V, Part2.VCC, R13.Pin_0
  N1: S1.3, R2.Pin_1
  N2: S1.4, Part1.D24
  N3: S2.3, R9.Pin_1
  N4: S2.4, Part1.D22
  N5: S3.3, R8.Pin_1
  N6: S3.4, Part1.D23
  N7: S4.3, R7.Pin_1
  N8: S4.4, Part1.D25
  N9: S5.3, R6.Pin_1
  N10: S5.4, Part1.D26
  GND: R1.leg1, U1.VSS, U1.R_W, U1.K, R2.Pin_0, R6.Pin_0, R7.Pin_0, R8.Pin_0, R9.Pin_0, Part1.GND, LED2.common_cathode, Part2.GND
  N11: R1.wiper, U1.VO
  N12: U1.RS, Part1.D7_PWM
  N13: U1.E, Part1.D6_PWM
  N14: U1.DB4, Part1.D5_PWM
  N15: U1.DB5, Part1.D4_PWM
  N16: U1.DB6, Part1.D3_PWM
  N17: U1.DB7, Part1.D2_PWM
  N18: U1.A, R13.Pin_1
  N19: Part1.D11_PWM, R10.Pin_0
  N20: Part1.D10_PWM, R11.Pin_0
  N21: Part1.D9_PWM, R12.Pin_0
  N22: Part1.D50, Part2.SCK
  N23: Part1.D51, Part2.MOSI
  N24: Part1.D52, Part2.MISO
  N25: Part1.D53, Part2.CS
  N26: R10.Pin_1, LED2.blue_anode
  N27: R11.Pin_1, LED2.green_anode
  N28: R12.Pin_1, LED2.red_anode
